# Fritzing sketch Schaltplan (saved by Fritzing 0.9.3b)

parts:
  Bauteil1 = Arduino Nano (Rev3.0)
  DFPlayer_Mini1 = DFPlayer MINI [package="DIP (Dual Inline) [THT]"]
  Q1 = Basic FET P-Channel [package="D2Pak [SMD]"]
  SP1 = SPEAKER [package=pcb_mount_speaker]
  82kOhm = Resistor [tolerance=±5% resistance=82k package="0805 [SMD]"]
  Q2 = NPN-Transistor [package="SOT-23 [SMD]"]
  C1 = Electrolytic Capacitor [capacitance=100µF package="200 mil [THT, electrolytic]"]
  Q3 = Basic FET N-Channel [part_number=SSM3K310T package="TO220 [THT]"]
  Back = Momentary Switch [package=ksa_sealed_tac_switch]
  Fwd = Momentary Switch [package=ksa_sealed_tac_switch]
  Volume_Down = Momentary Switch [package=ksa_sealed_tac_switch]
  Volume_Up = Momentary Switch [package=ksa_sealed_tac_switch]
  Play/Stop = Momentary Switch [package=ksa_sealed_tac_switch]
  5V = Battery
  82kOhm1 = Resistor [tolerance=±5% resistance=300 package="0805 [SMD]"]
  Q4 = Basic FET N-Channel [part_number=SSM3K310T package="TO220 [THT]"]
  82kOhm2 = Resistor [tolerance=±5% resistance=300 package="0805 [SMD]"]
  D1 = Rectifier Diode [part_number=1N4001 package="300 mil [THT]"]
  D2 = Rectifier Diode [package="300 mil [THT]"]
  82kOhm3 = Resistor [tolerance=±5% resistance=1k package="0805 [SMD]"]
  Bauteil2 = RFID-RC522-v3

nets:
  N1: Bauteil1.GND, Back.4, Fwd.4, Volume_Down.4, Volume_Up.4, Play/Stop.4
  N2: Bauteil1.D2, DFPlayer_Mini1.TX
  N3: Bauteil1.D3, 82kOhm3.Pin_1
  N4: Bauteil1.D4, DFPlayer_Mini1.BUSY
  N5: Bauteil1.D7, 82kOhm1.Pin_1
  N6: Bauteil1.D8, 82kOhm2.Pin_1
  N7: Bauteil1.D9, Bauteil2.GND
  N8: Bauteil1.D10, Bauteil2.SDA
  N9: Bauteil1.D11/MOSI, Bauteil2.MOSI
  N10: Bauteil1.D12/MISO, Bauteil2.MISO
  5V: Bauteil1.5V, DFPlayer_Mini1.VCC, Q1.source
  N11: Bauteil1.A4, Back.2
  N12: Bauteil1.A3, Fwd.2
  N13: Bauteil1.A2, Volume_Down.1
  N14: Bauteil1.A1, Volume_Up.2
  N15: Bauteil1.A0, D2.anode
  3V3: Bauteil1.3V3, Bauteil2.3.3V
  N16: Bauteil1.D13/SCK, Bauteil2.SCK
  N17: DFPlayer_Mini1.RX, 82kOhm3.Pin_0
  N18: DFPlayer_Mini1.SPK1, Q4.drain
  N19: DFPlayer_Mini1.GND, Q2.2, C1.-, 5V.+
  N20: DFPlayer_Mini1.SPK2, SP1.-
  N21: Q1.Gate, 82kOhm.Pin_0, Q2.1, C1.+, D1.anode
  N22: Q1.drain, 5V.-
  N23: SP1.+, Q3.drain
  N24: Q2.0, 82kOhm1.Pin_0
  N25: Q3.gate, Q4.gate, 82kOhm2.Pin_0
  N26: Q3.source, Q4.source
  N27: Play/Stop.2, D1.cathode, D2.cathode

notes:
  Changes to the original design:
  - Q1 is used to completely disconnect the power.
  - Since the software takes around 2 seconds to startup and pull the shutdown pin (D7) up, the capacitor C1 paypasses it for some seconds.
  - The diode D1 is needed so the pause button still can normally operate.
  - The diode D2 is to make sure in power off state there is no current flowing into the arduino while the Q1 is still partially open.
  - Q3 and Q4 are used to disconnect the speaker at startup, before shutdown and while nothing is played. This way there are no popping sounds and no noise in inde.

custom parts:
  DFPlayer MINI: MP3 module by DFRobot.com for playing Music from an SD-Card. Supports WAV and MP3 files.
  RFID-RC522-v3: A simple China made RFID-RC522 Reader (6x4 cm); do check the pin labels, as this is a MFRC522 based clone.
